// Logisim project rover32.circ as structural Verilog: 19 circuits, main circuit rvr32_alu
module rvr32_alu (
  input  [31:0] data_in1,
  input  [31:0] data_in2,
  input  [3:0] aluop,
  input  data_cmp,
  output [31:0] data_out
);

  wire [31:0] and_1_out, demultiplexer_1_out0, demultiplexer_1_out1, multiplexer_1_out, multiplexer_3_out,
       not_1_out, or_1_out, result0, result1, result3, xor_1_out;
  wire [32:0] shifter_1_out;
  wire [32:32] multiplexer_2_out;

  Multiplexer #(.width(32)) multiplexer_1 (
    .in0(data_in1),
    .in1({data_in1[0], data_in1[1], data_in1[2], data_in1[3], data_in1[4], data_in1[5], data_in1[6], data_in1[7], data_in1[8], data_in1[9], data_in1[10], data_in1[11], data_in1[12], data_in1[13], data_in1[14], data_in1[15], data_in1[16], data_in1[17], data_in1[18], data_in1[19], data_in1[20], data_in1[21], data_in1[22], data_in1[23], data_in1[24], data_in1[25], data_in1[26], data_in1[27], data_in1[28], data_in1[29], data_in1[30], data_in1[31]}),
    .out(multiplexer_1_out), .sel(aluop[3]));
  Multiplexer multiplexer_2 (.in0(1'b0), .in1(multiplexer_1_out[31]), .out(multiplexer_2_out[32]), .sel(aluop[2]));
  assign not_1_out = ~data_in2;  // NOT_Gate not_1, 32 bits wide
  Multiplexer #(.width(32)) multiplexer_3 (.in0(data_in2), .in1(not_1_out), .out(multiplexer_3_out), .sel(aluop[2]));
  Shifter #(.shift("ar"), .width(33)) shifter_1 (
    .in({multiplexer_2_out[32], multiplexer_1_out}), .\dist ({1'b0, data_in2[4:0]}), .out(shifter_1_out));
  Adder #(.width(32)) adder_1 (.a(data_in1), .b(multiplexer_3_out), .out(result0), .cin(aluop[2]));  // open: cout
  Demultiplexer #(.width(32)) demultiplexer_1 (
    .out0(demultiplexer_1_out0), .out1(demultiplexer_1_out1), .in(shifter_1_out[31:0]), .sel(aluop[3]));
  assign xor_1_out = data_in2 ^ data_in1;  // XOR_Gate xor_1, 32 bits wide
  assign or_1_out = data_in2 | data_in1;  // OR_Gate or_1, 32 bits wide
  assign and_1_out = data_in2 & data_in1;  // AND_Gate and_1, 32 bits wide
  Multiplexer #(.select(2), .width(32)) multiplexer_4 (
    .in0(data_in2), .in1(xor_1_out), .in2(or_1_out), .in3(and_1_out), .out(result3), .sel(aluop[3:2]));
  Multiplexer #(.width(32)) multiplexer_5 (
    .in0(demultiplexer_1_out0),
    .in1({demultiplexer_1_out1[0], demultiplexer_1_out1[1], demultiplexer_1_out1[2], demultiplexer_1_out1[3], demultiplexer_1_out1[4], demultiplexer_1_out1[5], demultiplexer_1_out1[6], demultiplexer_1_out1[7], demultiplexer_1_out1[8], demultiplexer_1_out1[9], demultiplexer_1_out1[10], demultiplexer_1_out1[11], demultiplexer_1_out1[12], demultiplexer_1_out1[13], demultiplexer_1_out1[14], demultiplexer_1_out1[15], demultiplexer_1_out1[16], demultiplexer_1_out1[17], demultiplexer_1_out1[18], demultiplexer_1_out1[19], demultiplexer_1_out1[20], demultiplexer_1_out1[21], demultiplexer_1_out1[22], demultiplexer_1_out1[23], demultiplexer_1_out1[24], demultiplexer_1_out1[25], demultiplexer_1_out1[26], demultiplexer_1_out1[27], demultiplexer_1_out1[28], demultiplexer_1_out1[29], demultiplexer_1_out1[30], demultiplexer_1_out1[31]}),
    .out(result1), .sel(aluop[3]));
  Multiplexer #(.select(2), .width(32)) multiplexer_6 (
    .in0(result0), .in1(result1), .in2({{31{1'b0}}, data_cmp}), .in3(result3), .out(data_out),
    .sel(aluop[1:0]));

  // Other names for the same wires on the sheet: aluop_1_0[1:0] = aluop[1:0]; aluop_2 = aluop[2];
  //   aluop_3_2[1:0] = aluop[3:2]; aluop_3 = aluop[3]; result2[0] = data_cmp;
  //   rev_data_in1[31:0] = {data_in1[0], data_in1[1], data_in1[2], data_in1[3], data_in1[4], data_in1[5], data_in1[6], data_in1[7], data_in1[8], data_in1[9], data_in1[10], data_in1[11], data_in1[12], data_in1[13], data_in1[14], data_in1[15], data_in1[16], data_in1[17], data_in1[18], data_in1[19], data_in1[20], data_in1[21], data_in1[22], data_in1[23], data_in1[24], data_in1[25], data_in1[26], data_in1[27], data_in1[28], data_in1[29], data_in1[30], data_in1[31]}
endmodule

module rvr32_localpc (
  input  [31:0] jdata,
  input  [31:0] bimm,
  input  jmp,
  input  br,
  input  we,
  input  clk,
  input  rst_n,
  output [31:0] pc_next,
  output [31:0] pc
);

  wire not_1_out;
  wire [31:0] multiplexer_1_out, multiplexer_2_out;

  not not_1 (not_1_out, rst_n);
  Multiplexer #(.width(32)) multiplexer_1 (.in0(pc_next), .in1(jdata), .out(multiplexer_1_out), .sel(jmp));
  Register #(.width(32)) r_pc (.D(multiplexer_1_out), .en(we), .clk(clk), .Q(pc), .clr(not_1_out));
  Multiplexer #(.width(32)) multiplexer_2 (.in0(32'h4), .in1(bimm), .out(multiplexer_2_out), .sel(br));
  Adder #(.width(32)) adder_1 (.a(pc), .b(multiplexer_2_out), .out(pc_next), .cin(1'b0));  // open: cout
endmodule

module rvr32_regfile (
  input  [4:0] addr_b,
  input  [4:0] addr_c,
  input  [31:0] wdata_a,
  input  clk,
  input  rst_n,
  input  we_a,
  input  [4:0] addr_a,
  output [31:0] rdata_c,
  output [31:0] rdata_b
);

  wire ctrl_a_we1, ctrl_a_we2, ctrl_a_we3, ctrl_a_we4, ctrl_a_we5, ctrl_a_we6, ctrl_a_we7, ctrl_a_we8,
       ctrl_a_we9, ctrl_a_we10, ctrl_a_we11, ctrl_a_we12, ctrl_a_we13, ctrl_a_we14, ctrl_a_we15, ctrl_a_we16,
       ctrl_a_we17, ctrl_a_we18, ctrl_a_we19, ctrl_a_we20, ctrl_a_we21, ctrl_a_we22, ctrl_a_we23,
       ctrl_a_we24, ctrl_a_we25, ctrl_a_we26, ctrl_a_we27, ctrl_a_we28, ctrl_a_we29, ctrl_a_we30,
       ctrl_a_we31, rst, undriven, undriven_2, undriven_3, undriven_4, undriven_5;
  wire [31:0] general_reg_1, general_reg_2, general_reg_3, general_reg_4, general_reg_5, general_reg_6,
       general_reg_7, general_reg_8, general_reg_9, general_reg_10, general_reg_11, general_reg_12,
       general_reg_13, general_reg_14, general_reg_15, general_reg_16, general_reg_17, general_reg_18,
       general_reg_19, general_reg_20, general_reg_21, general_reg_22, general_reg_23, general_reg_24,
       general_reg_25, general_reg_26, general_reg_27, general_reg_28, general_reg_29, general_reg_30,
       general_reg_31;

  Demultiplexer #(.select(5)) demultiplexer_1 (
    .out1(ctrl_a_we1), .out2(ctrl_a_we2), .out3(ctrl_a_we3), .out4(ctrl_a_we4), .out5(ctrl_a_we5),
    .out6(ctrl_a_we6), .out7(ctrl_a_we7), .out8(ctrl_a_we8), .out9(ctrl_a_we9), .out10(ctrl_a_we10),
    .out11(ctrl_a_we11), .out12(ctrl_a_we12), .out13(ctrl_a_we13), .out14(ctrl_a_we14), .out15(ctrl_a_we15),
    .out16(ctrl_a_we16), .out17(ctrl_a_we17), .out18(ctrl_a_we18), .out19(ctrl_a_we19), .out20(ctrl_a_we20),
    .out21(ctrl_a_we21), .out22(ctrl_a_we22), .out23(ctrl_a_we23), .out24(ctrl_a_we24), .out25(ctrl_a_we25),
    .out26(ctrl_a_we26), .out27(ctrl_a_we27), .out28(ctrl_a_we28), .out29(ctrl_a_we29), .out30(ctrl_a_we30),
    .out31(ctrl_a_we31), .in(we_a), .sel(addr_a));  // open: out0
  Multiplexer #(.select(5), .width(32)) multiplexer_1 (
    .in0({32{1'b0}}), .in1(general_reg_1), .in2(general_reg_2), .in3(general_reg_3), .in4(general_reg_4),
    .in5(general_reg_5), .in6(general_reg_6), .in7(general_reg_7), .in8(general_reg_8), .in9(general_reg_9),
    .in10(general_reg_10), .in11(general_reg_11), .in12(general_reg_12), .in13(general_reg_13),
    .in14(general_reg_14), .in15(general_reg_15), .in16(general_reg_16), .in17(general_reg_17),
    .in18(general_reg_18), .in19(general_reg_19), .in20(general_reg_20), .in21(general_reg_21),
    .in22(general_reg_22), .in23(general_reg_23), .in24(general_reg_24), .in25(general_reg_25),
    .in26(general_reg_26), .in27(general_reg_27), .in28(general_reg_28), .in29(general_reg_29),
    .in30(general_reg_30), .in31(general_reg_31), .out(rdata_b), .sel(addr_b));
  not not_1 (rst, rst_n);
  Register #(.width(32)) r_x4 (.D(wdata_a), .en(ctrl_a_we4), .clk(clk), .Q(general_reg_4), .clr(rst));
  Register #(.width(32)) r_x8 (.D(wdata_a), .en(ctrl_a_we8), .clk(clk), .Q(general_reg_8), .clr(rst));
  Register #(.width(32)) r_x12 (.D(wdata_a), .en(ctrl_a_we12), .clk(clk), .Q(general_reg_12), .clr(undriven));
  Register #(.width(32)) r_x16 (.D(wdata_a), .en(ctrl_a_we16), .clk(clk), .Q(general_reg_16), .clr(undriven_2));
  Register #(.width(32)) r_x20 (.D(wdata_a), .en(ctrl_a_we20), .clk(clk), .Q(general_reg_20), .clr(undriven_3));
  Register #(.width(32)) r_x24 (.D(wdata_a), .en(ctrl_a_we24), .clk(clk), .Q(general_reg_24), .clr(undriven_4));
  Register #(.width(32)) r_x28 (.D(wdata_a), .en(ctrl_a_we28), .clk(clk), .Q(general_reg_28), .clr(undriven_5));
  Register #(.width(32)) r_x1 (.D(wdata_a), .en(ctrl_a_we1), .clk(clk), .Q(general_reg_1), .clr(rst));
  Register #(.width(32)) r_x5 (.D(wdata_a), .en(ctrl_a_we5), .clk(clk), .Q(general_reg_5), .clr(rst));
  Register #(.width(32)) r_x9 (.D(wdata_a), .en(ctrl_a_we9), .clk(clk), .Q(general_reg_9), .clr(rst));
  Register #(.width(32)) r_x13 (.D(wdata_a), .en(ctrl_a_we13), .clk(clk), .Q(general_reg_13), .clr(rst));
  Register #(.width(32)) r_x17 (.D(wdata_a), .en(ctrl_a_we17), .clk(clk), .Q(general_reg_17), .clr(rst));
  Register #(.width(32)) r_x21 (.D(wdata_a), .en(ctrl_a_we21), .clk(clk), .Q(general_reg_21), .clr(rst));
  Register #(.width(32)) r_x25 (.D(wdata_a), .en(ctrl_a_we25), .clk(clk), .Q(general_reg_25), .clr(rst));
  Register #(.width(32)) r_x29 (.D(wdata_a), .en(ctrl_a_we29), .clk(clk), .Q(general_reg_29), .clr(rst));
  Register #(.width(32)) r_x2 (.D(wdata_a), .en(ctrl_a_we2), .clk(clk), .Q(general_reg_2), .clr(rst));
  Register #(.width(32)) r_x6 (.D(wdata_a), .en(ctrl_a_we6), .clk(clk), .Q(general_reg_6), .clr(rst));
  Register #(.width(32)) r_x10 (.D(wdata_a), .en(ctrl_a_we10), .clk(clk), .Q(general_reg_10), .clr(rst));
  Register #(.width(32)) r_x14 (.D(wdata_a), .en(ctrl_a_we14), .clk(clk), .Q(general_reg_14), .clr(rst));
  Register #(.width(32)) r_x18 (.D(wdata_a), .en(ctrl_a_we18), .clk(clk), .Q(general_reg_18), .clr(rst));
  Register #(.width(32)) r_x22 (.D(wdata_a), .en(ctrl_a_we22), .clk(clk), .Q(general_reg_22), .clr(rst));
  Register #(.width(32)) r_x26 (.D(wdata_a), .en(ctrl_a_we26), .clk(clk), .Q(general_reg_26), .clr(rst));
  Register #(.width(32)) r_x30 (.D(wdata_a), .en(ctrl_a_we30), .clk(clk), .Q(general_reg_30), .clr(rst));
  Register #(.width(32)) r_x3 (.D(wdata_a), .en(ctrl_a_we3), .clk(clk), .Q(general_reg_3), .clr(rst));
  Register #(.width(32)) r_x7 (.D(wdata_a), .en(ctrl_a_we7), .clk(clk), .Q(general_reg_7), .clr(rst));
  Register #(.width(32)) r_x11 (.D(wdata_a), .en(ctrl_a_we11), .clk(clk), .Q(general_reg_11), .clr(rst));
  Register #(.width(32)) r_x15 (.D(wdata_a), .en(ctrl_a_we15), .clk(clk), .Q(general_reg_15), .clr(rst));
  Register #(.width(32)) r_x19 (.D(wdata_a), .en(ctrl_a_we19), .clk(clk), .Q(general_reg_19), .clr(rst));
  Register #(.width(32)) r_x23 (.D(wdata_a), .en(ctrl_a_we23), .clk(clk), .Q(general_reg_23), .clr(rst));
  Register #(.width(32)) r_x27 (.D(wdata_a), .en(ctrl_a_we27), .clk(clk), .Q(general_reg_27), .clr(rst));
  Register #(.width(32)) r_x31 (.D(wdata_a), .en(ctrl_a_we31), .clk(clk), .Q(general_reg_31), .clr(rst));
  Multiplexer #(.select(5), .width(32)) multiplexer_2 (
    .in0({32{1'b0}}), .in1(general_reg_1), .in2(general_reg_2), .in3(general_reg_3), .in4(general_reg_4),
    .in5(general_reg_5), .in6(general_reg_6), .in7(general_reg_7), .in8(general_reg_8), .in9(general_reg_9),
    .in10(general_reg_10), .in11(general_reg_11), .in12(general_reg_12), .in13(general_reg_13),
    .in14(general_reg_14), .in15(general_reg_15), .in16(general_reg_16), .in17(general_reg_17),
    .in18(general_reg_18), .in19(general_reg_19), .in20(general_reg_20), .in21(general_reg_21),
    .in22(general_reg_22), .in23(general_reg_23), .in24(general_reg_24), .in25(general_reg_25),
    .in26(general_reg_26), .in27(general_reg_27), .in28(general_reg_28), .in29(general_reg_29),
    .in30(general_reg_30), .in31(general_reg_31), .out(rdata_c), .sel(addr_c));

  // Other names for the same wires on the sheet: data_a[31:0] = wdata_a
endmodule

module rvr32_cmp (
  input  [31:0] data_in1,
  input  [31:0] data_in2,
  input  [2:0] cmpop,
  output data_out
);

  wire comparator_1_eq, comparator_1_lt, multiplexer_3_out, not_1_out, not_2_out, not_3_out;
  wire [31:31] multiplexer_1_out, multiplexer_2_out;

  not not_1 (not_1_out, data_in1[31]);
  not not_2 (not_2_out, data_in2[31]);
  Multiplexer multiplexer_1 (.in0(not_1_out), .in1(data_in1[31]), .out(multiplexer_1_out[31]), .sel(cmpop[1]));
  Multiplexer multiplexer_2 (.in0(not_2_out), .in1(data_in2[31]), .out(multiplexer_2_out[31]), .sel(cmpop[1]));
  Comparator #(.mode("unsigned"), .width(32)) comparator_1 (
    .a({multiplexer_1_out[31], data_in1[30:0]}), .b({multiplexer_2_out[31], data_in2[30:0]}),
    .eq(comparator_1_eq), .lt(comparator_1_lt));  // open: gt
  Multiplexer multiplexer_3 (.in0(comparator_1_eq), .in1(comparator_1_lt), .out(multiplexer_3_out), .sel(cmpop[2]));
  not not_3 (not_3_out, multiplexer_3_out);
  Multiplexer multiplexer_4 (.in0(multiplexer_3_out), .in1(not_3_out), .out(data_out), .sel(cmpop[0]));

  // Other names for the same wires on the sheet: cmpop_0 = cmpop[0]; cmpop_1 = cmpop[1]; cmpop_2 = cmpop[2]
endmodule

module rvr32_ealu (
  input  [31:0] data_in1,
  input  [31:0] data_in2,
  input  [2:0] ealuop,
  output [31:0] data_out
);

  wire and_1_out, or_1_out;
  wire [32:0] multiplier_1_cout, multiplier_1_out;
  wire [32:32] multiplexer_1_out, multiplexer_2_out;

  and and_1 (and_1_out, ealuop[0], ealuop[1]);
  Multiplexer multiplexer_1 (.in0(data_in1[31]), .in1(1'b0), .out(multiplexer_1_out[32]), .sel(and_1_out));
  Multiplexer multiplexer_2 (.in0(data_in2[31]), .in1(1'b0), .out(multiplexer_2_out[32]), .sel(ealuop[1]));
  Multiplier #(.mode("twosComplement"), .width(33)) multiplier_1 (
    .a({multiplexer_1_out[32], data_in1}), .b({multiplexer_2_out[32], data_in2}), .out(multiplier_1_out),
    .cin({33{1'b0}}), .cout(multiplier_1_cout));
  // Probe on data_out
  Multiplexer #(.width(32)) multiplexer_3 (
    .in0(multiplier_1_out[31:0]), .in1({multiplier_1_cout[30:0], multiplier_1_out[32]}), .out(data_out),
    .sel(or_1_out));
  or or_1 (or_1_out, ealuop[0], ealuop[1]);

  // Other names for the same wires on the sheet: ealuop_0 = ealuop[0]; ealuop_1 = ealuop[1]; ealuop_2 = ealuop[2]
endmodule

module rvr32_lsu (
  input  [31:0] addr,
  input  [31:0] wdata,
  input  [3:0] lsuop,
  input  [31:0] mem_rdata,
  input  req,
  input  clk,
  input  rst_n,
  input  mem_ready,
  output [31:0] mem_addr,
  output [31:0] mem_wdata,
  output [3:0] mem_wstrb,
  output [31:0] rdata,
  output mem_valid,
  output ready
);

  wire and_1_out, and_3_out, and_4_out, and_5_out, and_6_out, and_7_out, and_8_out, mem_wstrb_0, mem_wstrb_1,
       mem_wstrb_2, mem_wstrb_3, multiplexer_1_out, not_1_out, not_2_out, or_2_out, or_7_out, r_req_past_q,
       r_req_q;
  wire [0:0] or_1_out;
  wire [7:0] multiplexer_4_out, multiplexer_8_out;
  wire [7:7] ext8;

  not not_1 (not_1_out, rst_n);
  or or_1 (or_1_out[0], addr[0], lsuop[0]);
  Multiplexer #(.select(2)) multiplexer_1 (
    .in0(mem_rdata[7]), .in1(mem_rdata[15]), .in2(mem_rdata[23]), .in3(mem_rdata[31]),
    .out(multiplexer_1_out), .sel({addr[1], or_1_out[0]}));
  Register #(.width(1)) r_req (.D(and_1_out), .en(1'b1), .clk(clk), .Q(r_req_q), .clr(not_1_out));
  and and_1 (and_1_out, req, ~ready);  // AND_Gate
  Multiplexer multiplexer_2 (.in0(multiplexer_1_out), .in1(1'b0), .out(ext8[7]), .sel(lsuop[2]));
  not not_2 (not_2_out, clk);
  Multiplexer #(.select(2), .width(8)) multiplexer_3 (
    .in0(mem_rdata[7:0]), .in1(mem_rdata[15:8]), .in2(mem_rdata[23:16]), .in3(mem_rdata[31:24]),
    .out(rdata[7:0]), .sel(addr[1:0]));
  Multiplexer #(.width(8)) multiplexer_4 (
    .in0(mem_rdata[15:8]), .in1(mem_rdata[31:24]), .out(multiplexer_4_out), .sel(addr[1]));
  Multiplexer #(.width(8)) multiplexer_5 (
    .in0({8{ext8[7]}}), .in1(mem_rdata[31:24]), .out(rdata[31:24]), .sel(lsuop[1]));
  Register #(.width(1)) r_req_past (.D(r_req_q), .en(1'b1), .clk(not_2_out), .Q(r_req_past_q), .clr(not_1_out));
  or or_2 (or_2_out, lsuop[0], lsuop[1]);
  Multiplexer #(.width(8)) multiplexer_6 (
    .in0({8{ext8[7]}}), .in1(multiplexer_4_out), .out(rdata[15:8]), .sel(or_2_out));
  Multiplexer #(.width(8)) multiplexer_7 (
    .in0({8{ext8[7]}}), .in1(mem_rdata[23:16]), .out(rdata[23:16]), .sel(lsuop[1]));
  and and_2 (ready, r_req_past_q, mem_ready);
  nor nor_1 (mem_wstrb_0, addr[0], addr[1]);
  and and_3 (and_3_out, addr[0], ~addr[1]);  // AND_Gate
  or or_3 (mem_wstrb_1, and_3_out, and_4_out, lsuop[1]);
  and and_4 (and_4_out, ~addr[1], lsuop[0]);  // AND_Gate
  and and_5 (and_5_out, ~addr[0], addr[1]);  // AND_Gate
  or or_4 (mem_wstrb_2, and_5_out, and_6_out, lsuop[1]);
  and and_6 (and_6_out, addr[1], lsuop[0]);
  and and_7 (and_7_out, addr[0], addr[1]);
  or or_5 (mem_wstrb_3, and_7_out, and_8_out, lsuop[1]);
  and and_8 (and_8_out, addr[1], lsuop[0]);
  or or_6 (mem_valid, r_req_q, r_req_past_q);
  and and_9 (mem_wstrb[0], lsuop[3], mem_wstrb_0);
  and and_10 (mem_wstrb[1], lsuop[3], mem_wstrb_1);
  and and_11 (mem_wstrb[2], lsuop[3], mem_wstrb_2);
  and and_12 (mem_wstrb[3], lsuop[3], mem_wstrb_3);
  Multiplexer #(.width(8)) multiplexer_8 (.in0(wdata[7:0]), .in1(wdata[15:8]), .out(multiplexer_8_out), .sel(lsuop[0]));
  Multiplexer #(.width(8)) multiplexer_9 (
    .in0(multiplexer_8_out), .in1(wdata[31:24]), .out(mem_wdata[31:24]), .sel(lsuop[1]));
  or or_7 (or_7_out, lsuop[0], lsuop[1]);
  Multiplexer #(.width(8)) multiplexer_10 (.in0(wdata[7:0]), .in1(wdata[15:8]), .out(mem_wdata[15:8]), .sel(or_7_out));
  Multiplexer #(.width(8)) multiplexer_11 (
    .in0(wdata[7:0]), .in1(wdata[23:16]), .out(mem_wdata[23:16]), .sel(lsuop[1]));

  assign mem_addr = addr;
  assign mem_wdata[7:0] = wdata[7:0];

  // Other names for the same wires on the sheet: ext8[6:0] = {7{ext8[7]}}; lsuop_0 = lsuop[0]; lsuop_1 = lsuop[1];
  //   lsuop_2 = lsuop[2]; lsuop_3 = lsuop[3]; addr_0 = addr[0]; addr_1_0[1:0] = addr[1:0]; addr_1 = addr[1];
  //   mem_wdata_7_0[7:0] = wdata[7:0]; wdata_7_0[7:0] = wdata[7:0]; mem_wdata_15_8[7:0] = mem_wdata[15:8];
  //   mem_wdata_23_16[7:0] = mem_wdata[23:16]; mem_wdata_31_24[7:0] = mem_wdata[31:24]; rdata_7_0[7:0] = rdata[7:0];
  //   rdata_15_8[7:0] = rdata[15:8]; rdata_23_16[7:0] = rdata[23:16]; rdata_31_24[7:0] = rdata[31:24];
  //   wdata_15_8[7:0] = wdata[15:8]; wdata_23_16[7:0] = wdata[23:16]; wdata_31_24[7:0] = wdata[31:24]
endmodule

module rvr32_sp (
  input  [14:0] rsd,
  input  start,
  input  clk,
  input  rst_n,
  input  [23:0] sp_uop,
  input  [31:0] imm,
  input  sync_ready,
  input  inst_ready,
  input  [31:0] shared_pc,
  input  [31:0] mem_rdata,
  input  [31:0] spid,
  input  mem_ready,
  output wfi,
  output wfs,
  output exec,
  output brc,
  output [31:0] pc,
  output [31:0] mem_addr,
  output [31:0] mem_wdata,
  output [3:0] mem_wstrb,
  output mem_valid
);

  wire and_1_out, and_2_out, and_3_out, and_4_out, and_5_out, and_6_out, and_7_out, comparator_1_eq,
       mem_exec, not_1_out, not_2_out, not_3_out, not_4_out, not_5_out, not_6_out, or_1_out, or_3_out,
       or_4_out, r_sync_q, r_work_q, ready, state_work;
  wire [31:0] data_rs1, data_rs2, multiplexer_1_out, multiplexer_2_out, multiplexer_3_out, multiplexer_4_out,
       pc_next, u_alu_data_out, u_ealu_data_out, u_lsu_rdata;

  or or_1 (or_1_out, ~sp_uop[15], sync_ready);  // OR_Gate
  and and_1 (and_1_out, exec, mem_exec, or_1_out);
  and and_2 (and_2_out, sp_uop[20], exec, mem_exec);
  or or_2 (mem_exec, sp_uop[18], sp_uop[19], ready);
  and and_3 (and_3_out, brc, sp_uop[22]);
  not not_1 (not_1_out, and_4_out);
  and and_4 (and_4_out, sp_uop[14], exec);
  and and_5 (and_5_out, sp_uop[15], exec);
  rvr32_localpc rvr32_localpc_1 (
    .jmp(sp_uop[23]), .we(and_1_out), .clk(clk), .rst_n(state_work), .jdata(u_alu_data_out), .br(and_3_out),
    .bimm(imm), .pc(pc), .pc_next(pc_next));
  rvr32_regfile rvr32_regfile_1 (
    .clk(clk), .rst_n(state_work), .wdata_a(multiplexer_4_out), .addr_c(rsd[14:10]), .addr_b(rsd[9:5]),
    .we_a(and_2_out), .addr_a(rsd[4:0]), .rdata_b(data_rs1), .rdata_c(data_rs2));
  Register #(.width(1)) r_work (.D(not_1_out), .en(or_3_out), .clk(clk), .Q(r_work_q), .clr(not_2_out));
  or or_3 (or_3_out, start, and_4_out);
  not not_2 (not_2_out, rst_n);
  Register #(.width(1)) r_sync (.D(not_3_out), .en(or_4_out), .clk(clk), .Q(r_sync_q), .clr(not_4_out));
  not not_3 (not_3_out, sync_ready);
  or or_4 (or_4_out, sync_ready, and_5_out);
  not not_4 (not_4_out, state_work);
  and and_6 (and_6_out, state_work, inst_ready, comparator_1_eq);
  Comparator #(.mode("unsigned"), .width(32)) comparator_1 (
    .a(shared_pc), .b(pc), .eq(comparator_1_eq));  // open: gt, lt
  Register #(.width(1)) r_work_past (.D(r_work_q), .en(1'b1), .clk(not_5_out), .Q(state_work), .clr(not_2_out));
  not not_5 (not_5_out, clk);
  Register #(.width(1)) r_sync_past (.D(r_sync_q), .en(1'b1), .clk(not_6_out), .Q(wfs), .clr(not_4_out));
  not not_6 (not_6_out, clk);
  Register #(.width(1)) r_exec (.D(and_6_out), .en(1'b1), .clk(not_6_out), .Q(exec), .clr(not_4_out));
  Multiplexer #(.width(32)) multiplexer_1 (.in0(pc), .in1(data_rs1), .out(multiplexer_1_out), .sel(sp_uop[16]));
  Multiplexer #(.width(32)) multiplexer_2 (.in0(imm), .in1(data_rs2), .out(multiplexer_2_out), .sel(sp_uop[17]));
  and and_7 (and_7_out, ~sp_uop[18], ~sp_uop[19], exec);  // AND_Gate
  not not_7 (wfi, state_work);
  rvr32_cmp u_cmp (.data_in1(data_rs1), .data_in2(multiplexer_2_out), .cmpop(sp_uop[6:4]), .data_out(brc));
  rvr32_alu u_alu (
    .aluop(sp_uop[13:10]), .data_in2(multiplexer_2_out), .data_in1(multiplexer_1_out), .data_cmp(brc),
    .data_out(u_alu_data_out));
  rvr32_ealu u_ealu (.ealuop(sp_uop[9:7]), .data_in1(data_rs1), .data_in2(data_rs2), .data_out(u_ealu_data_out));
  rvr32_lsu u_lsu (
    .req(and_7_out), .clk(clk), .rst_n(state_work), .mem_ready(mem_ready), .mem_rdata(mem_rdata),
    .lsuop(sp_uop[3:0]), .addr(u_alu_data_out), .wdata(data_rs2), .mem_wstrb(mem_wstrb), .mem_addr(mem_addr),
    .ready(ready), .mem_valid(mem_valid), .mem_wdata(mem_wdata), .rdata(u_lsu_rdata));
  Multiplexer #(.width(32)) multiplexer_3 (
    .in0(u_alu_data_out), .in1(u_ealu_data_out), .out(multiplexer_3_out), .sel(sp_uop[21]));
  // Probe on multiplexer_3_out
  Multiplexer #(.select(2), .width(32)) multiplexer_4 (
    .in0(u_lsu_rdata), .in1(multiplexer_3_out), .in2(pc_next), .in3(spid), .out(multiplexer_4_out),
    .sel(sp_uop[19:18]));

  // Other names for the same wires on the sheet: spop[9:0] = sp_uop[23:14]; spop_4 = sp_uop[18]; spop_5 = sp_uop[19];
  //   rd[4:0] = rsd[4:0]; rs1[4:0] = rsd[9:5]; rs2[4:0] = rsd[14:10]; lsuop[3:0] = sp_uop[3:0];
  //   cmpop[2:0] = sp_uop[6:4]; ealuop[2:0] = sp_uop[9:7]; aluop[3:0] = sp_uop[13:10]; spop_0 = sp_uop[14];
  //   spop_1 = sp_uop[15]; spop_2 = sp_uop[16]; spop_3 = sp_uop[17]; spop_6 = sp_uop[20]; spop_7 = sp_uop[21];
  //   spop_8 = sp_uop[22]; spop_9 = sp_uop[23]; state_sync = wfs
endmodule

module rvr32_lsa_2p (
  input  [31:0] mem_rdata,
  input  valid0,
  input  [31:0] addr0,
  input  [31:0] addr1,
  input  valid1,
  input  [3:0] wstrb0,
  input  [3:0] wstrb1,
  input  clk,
  input  [31:0] wdata0,
  input  [31:0] wdata1,
  input  rst_n,
  input  mem_ready,
  output [31:0] rdata,
  output [31:0] mem_addr,
  output mem_valid,
  output [3:0] mem_wstrb,
  output [31:0] mem_wdata,
  output ready0,
  output ready1
);

  wire and_1_out, ctrl_sel, ctrl_sel_valid, demultiplexer_1_out0, demultiplexer_1_out1, not_1_out, not_2_out,
       not_3_out;

  Multiplexer multiplexer_1 (.in0(valid0), .in1(valid1), .out(ctrl_sel), .sel(ctrl_sel_valid));
  not not_1 (not_1_out, ctrl_sel);
  not not_2 (not_2_out, valid0);
  and and_1 (and_1_out, mem_valid, rst_n);
  Demultiplexer #(.enable("true")) demultiplexer_1 (
    .out0(demultiplexer_1_out0), .out1(demultiplexer_1_out1), .in(mem_ready), .sel(ctrl_sel_valid),
    .en(mem_valid));
  Register #(.width(1)) register_1 (.D(not_2_out), .en(not_1_out), .clk(clk), .Q(ctrl_sel_valid), .clr(not_3_out));
  not not_3 (not_3_out, and_1_out);
  and and_2 (ready0, valid0, demultiplexer_1_out0);
  and and_3 (ready1, demultiplexer_1_out1, valid1);
  or or_1 (mem_valid, valid0, valid1);
  Multiplexer #(.enable("true"), .width(32)) multiplexer_2 (
    .in0(addr0), .in1(addr1), .out(mem_addr), .sel(ctrl_sel_valid), .en(mem_valid));
  Multiplexer #(.enable("true"), .width(4)) multiplexer_3 (
    .in0(wstrb0), .in1(wstrb1), .out(mem_wstrb), .sel(ctrl_sel_valid), .en(mem_valid));
  Multiplexer #(.enable("true"), .width(32)) multiplexer_4 (
    .in0(wdata0), .in1(wdata1), .out(mem_wdata), .sel(ctrl_sel_valid), .en(mem_valid));

  assign rdata = mem_rdata;
endmodule

module rvr32_immgen (
  input  [31:0] data_inst,
  input  type_b,
  input  type_s,
  input  type_u,
  input  type_j,
  output [31:0] data_out
);

  wire multiplexer_3_out, multiplexer_6_out, multiplexer_8_out, type_sb, type_uj, type_ujb;
  wire [3:0] multiplexer_1_out;

  Multiplexer #(.width(4)) multiplexer_1 (
    .in0(data_inst[24:21]), .in1(data_inst[11:8]), .out(multiplexer_1_out), .sel(type_sb));
  Multiplexer #(.width(6)) multiplexer_2 (.in0(data_inst[30:25]), .in1({6{1'b0}}), .out(data_out[10:5]), .sel(type_u));
  Multiplexer multiplexer_3 (.in0(data_inst[31]), .in1(data_inst[7]), .out(multiplexer_3_out), .sel(type_b));
  Multiplexer #(.width(8)) multiplexer_4 (
    .in0({8{data_inst[31]}}), .in1(data_inst[19:12]), .out(data_out[19:12]), .sel(type_uj));
  Multiplexer #(.width(12)) multiplexer_5 (
    .in0({12{data_inst[31]}}), .in1(data_inst[31:20]), .out(data_out[31:20]), .sel(type_u));
  or or_1 (type_uj, type_u, type_j);
  or or_2 (type_ujb, type_uj, type_b);
  or or_3 (type_sb, type_s, type_b);
  and and_1 (data_out[0], ~type_ujb, multiplexer_6_out);  // AND_Gate
  Multiplexer multiplexer_6 (.in0(data_inst[20]), .in1(data_inst[7]), .out(multiplexer_6_out), .sel(type_s));
  Multiplexer #(.width(4)) multiplexer_7 (.in0(multiplexer_1_out), .in1(4'b0000), .out(data_out[4:1]), .sel(type_u));
  Multiplexer multiplexer_8 (.in0(multiplexer_3_out), .in1(data_inst[20]), .out(multiplexer_8_out), .sel(type_j));
  Multiplexer multiplexer_9 (.in0(multiplexer_8_out), .in1(1'b0), .out(data_out[11]), .sel(type_u));

  // Other names for the same wires on the sheet: data_inst_8 = data_inst[8]; data_inst_9 = data_inst[9];
  //   data_inst_10 = data_inst[10]; data_inst_11 = data_inst[11]; data_inst_12 = data_inst[12];
  //   data_inst_13 = data_inst[13]; data_inst_14 = data_inst[14]; data_inst_15 = data_inst[15];
  //   data_inst_16 = data_inst[16]; data_inst_17 = data_inst[17]; data_inst_18 = data_inst[18];
  //   data_inst_19 = data_inst[19]; data_inst_20 = data_inst[20]; data_inst_21 = data_inst[21];
  //   data_inst_22 = data_inst[22]; data_inst_23 = data_inst[23]; data_inst_24 = data_inst[24];
  //   data_inst_25 = data_inst[25]; data_inst_26 = data_inst[26]; data_inst_27 = data_inst[27];
  //   data_inst_28 = data_inst[28]; data_inst_29 = data_inst[29]; data_inst_30 = data_inst[30];
  //   data_inst_31 = data_inst[31]; data_inst_7 = data_inst[7]; imm_0 = data_out[0]; imm_4_1[3:0] = data_out[4:1];
  //   imm_10_5[5:0] = data_out[10:5]; imm_11 = data_out[11]; imm_19_12[7:0] = data_out[19:12];
  //   imm_31_20[11:0] = data_out[31:20]
endmodule

module rvr32_lsa_4p (
  input  [31:0] mem_rdata,
  input  mem_ready,
  input  [31:0] addr0,
  input  [31:0] addr1,
  input  [31:0] addr2,
  input  [31:0] addr3,
  input  [3:0] wstrb0,
  input  [3:0] wstrb1,
  input  [3:0] wstrb2,
  input  [3:0] wstrb3,
  input  [31:0] wdata0,
  input  [31:0] wdata1,
  input  [31:0] wdata2,
  input  [31:0] wdata3,
  input  valid0,
  input  clk,
  input  valid1,
  input  valid2,
  input  valid3,
  input  rst_n,
  output [31:0] rdata,
  output mem_valid,
  output ready0,
  output ready1,
  output ready2,
  output ready3,
  output [31:0] mem_addr,
  output [3:0] mem_wstrb,
  output [31:0] mem_wdata
);

  wire and_1_out, and_2_out, and_7_out, and_8_out, and_9_out, and_10_out, and_11_out, and_12_out, and_13_out,
       ctrl_sel, demultiplexer_1_out0, demultiplexer_1_out1, demultiplexer_1_out2, demultiplexer_1_out3,
       nor_1_out, not_1_out, not_2_out, not_3_out, not_4_out, not_5_out, not_6_out, not_7_out, not_8_out,
       not_9_out, not_10_out, not_11_out, not_12_out, not_13_out, or_2_out, Q1, Q2;
  wire [1:0] ctrl_sel_valid;

  Demultiplexer #(.enable("true"), .select(2)) demultiplexer_1 (
    .out0(demultiplexer_1_out0), .out1(demultiplexer_1_out1), .out2(demultiplexer_1_out2),
    .out3(demultiplexer_1_out3), .in(mem_ready), .sel(ctrl_sel_valid), .en(mem_valid));
  Multiplexer #(.select(2)) multiplexer_1 (
    .in0(valid0), .in1(valid1), .in2(valid2), .in3(valid3), .out(ctrl_sel), .sel(ctrl_sel_valid));
  not not_1 (not_1_out, ctrl_sel);
  not not_2 (not_2_out, ctrl_sel);
  Multiplexer #(.enable("true"), .select(2), .width(32)) multiplexer_2 (
    .in0(addr0), .in1(addr1), .in2(addr2), .in3(addr3), .out(mem_addr), .sel(ctrl_sel_valid), .en(mem_valid));
  Multiplexer #(.enable("true"), .select(2), .width(4)) multiplexer_3 (
    .in0(wstrb0), .in1(wstrb1), .in2(wstrb2), .in3(wstrb3), .out(mem_wstrb), .sel(ctrl_sel_valid),
    .en(mem_valid));
  Multiplexer #(.enable("true"), .select(2), .width(32)) multiplexer_4 (
    .in0(wdata0), .in1(wdata1), .in2(wdata2), .in3(wdata3), .out(mem_wdata), .sel(ctrl_sel_valid),
    .en(mem_valid));
  // Probe on ctrl_sel_valid
  // Probe on Q1
  // Probe on Q2
  Register #(.width(1)) register_1 (.D(Q2), .en(not_1_out), .clk(clk), .Q(ctrl_sel_valid[1]), .clr(not_3_out));
  and and_1 (and_1_out, rst_n, mem_valid);
  not not_3 (not_3_out, and_1_out);
  Register #(.width(1)) register_2 (.D(Q1), .en(not_2_out), .clk(clk), .Q(ctrl_sel_valid[0]), .clr(not_4_out));
  and and_2 (and_2_out, rst_n, mem_valid);
  not not_4 (not_4_out, and_2_out);
  or or_1 (mem_valid, valid0, valid1, valid2, valid3);
  and and_3 (ready0, valid0, demultiplexer_1_out0);
  and and_4 (ready1, demultiplexer_1_out1, valid1);
  and and_5 (ready2, demultiplexer_1_out2, valid2);
  and and_6 (ready3, demultiplexer_1_out3, valid3);
  or or_2 (or_2_out, ctrl_sel_valid[1], ctrl_sel_valid[0]);
  not not_5 (not_5_out, valid1);
  not not_6 (not_6_out, valid1);
  not not_7 (not_7_out, ctrl_sel_valid[1]);
  nor nor_1 (nor_1_out, valid0, valid1);
  and and_7 (and_7_out, valid0, valid2, not_6_out, ctrl_sel_valid[0], not_7_out);
  and and_8 (and_8_out, valid1, valid3, ctrl_sel_valid[1]);
  and and_9 (and_9_out, or_2_out, valid3, valid0, not_5_out);
  or or_3 (Q2, nor_1_out, and_8_out, and_9_out, and_7_out);
  not not_8 (not_8_out, valid1);
  not not_9 (not_9_out, valid2);
  not not_10 (not_10_out, valid0);
  not not_11 (not_11_out, valid1);
  not not_12 (not_12_out, valid2);
  not not_13 (not_13_out, valid0);
  and and_10 (and_10_out, not_13_out, valid1);
  and and_11 (and_11_out, valid0, valid1, valid3);
  and and_12 (and_12_out, valid0, not_8_out, valid3, not_9_out);
  and and_13 (and_13_out, not_10_out, not_11_out, not_12_out);
  or or_4 (Q1, and_13_out, and_10_out, and_11_out, and_12_out);

  assign rdata = mem_rdata;

  // Other names for the same wires on the sheet: ctrl_sel_validl = ctrl_sel_valid[0];
  //   ctrl_sel_validh = ctrl_sel_valid[1]
endmodule

module rvr32_sharedpc (
  input  [31:0] jdata,
  input  jmp,
  input  we,
  input  clk,
  input  rst_n,
  input  [31:0] bjimm,
  input  brj,
  output [31:0] pc
);

  wire not_1_out;
  wire [31:0] adder_1_out, multiplexer_1_out, multiplexer_2_out;

  not not_1 (not_1_out, rst_n);
  Multiplexer #(.width(32)) multiplexer_1 (.in0(adder_1_out), .in1(jdata), .out(multiplexer_1_out), .sel(jmp));
  Register #(.width(32)) r_pc (.D(multiplexer_1_out), .en(we), .clk(clk), .Q(pc), .clr(not_1_out));
  // Probe on adder_1_out
  Multiplexer #(.width(32)) multiplexer_2 (.in0(32'h4), .in1(bjimm), .out(multiplexer_2_out), .sel(brj));
  Adder #(.width(32)) adder_1 (.a(pc), .b(multiplexer_2_out), .out(adder_1_out), .cin(1'b0));  // open: cout
endmodule

module rvr32_pca_4p (
  input  idle0,
  input  idle1,
  input  idle2,
  input  idle3,
  input  [31:0] pc0,
  input  [31:0] pc1,
  input  [31:0] pc2,
  input  [31:0] pc3,
  input  req,
  input  clk,
  input  rst_n,
  output [31:0] min_pc,
  output ready
);

  wire and_1_out, not_1_out, not_2_out, r_jalr_q, t_pc, t_pc01, t_pc23;
  wire [31:0] multiplexer_1_out, multiplexer_2_out;
  wire [32:0] multiplexer_4_out, multiplexer_5_out;

  Register #(.width(1)) r_jalr (.D(and_1_out), .en(1'b1), .clk(clk), .Q(r_jalr_q), .clr(not_1_out));
  and and_1 (and_1_out, ~ready, req);  // AND_Gate
  not not_1 (not_1_out, rst_n);
  Multiplexer #(.width(32)) multiplexer_1 (.in0(pc0), .in1(pc1), .out(multiplexer_1_out), .sel(t_pc01));
  Multiplexer #(.width(32)) multiplexer_2 (.in0(pc2), .in1(pc3), .out(multiplexer_2_out), .sel(t_pc23));
  not not_2 (not_2_out, clk);
  Comparator #(.mode("unsigned"), .width(33)) comparator_1 (
    .a({idle0, pc0}), .b({idle1, pc1}), .gt(t_pc01));  // open: eq, lt
  Comparator #(.mode("unsigned"), .width(33)) comparator_2 (
    .a({idle2, pc2}), .b({idle3, pc3}), .gt(t_pc23));  // open: eq, lt
  Multiplexer #(.width(32)) multiplexer_3 (.in0(multiplexer_1_out), .in1(multiplexer_2_out), .out(min_pc), .sel(t_pc));
  Register #(.width(1)) r_jalr_past (.D(r_jalr_q), .en(1'b1), .clk(not_2_out), .Q(ready), .clr(not_1_out));
  Multiplexer #(.width(33)) multiplexer_4 (
    .in0({idle0, pc0}), .in1({idle1, pc1}), .out(multiplexer_4_out), .sel(t_pc01));
  Multiplexer #(.width(33)) multiplexer_5 (
    .in0({idle2, pc2}), .in1({idle3, pc3}), .out(multiplexer_5_out), .sel(t_pc23));
  Comparator #(.mode("unsigned"), .width(33)) comparator_3 (
    .a(multiplexer_4_out), .b(multiplexer_5_out), .gt(t_pc));  // open: eq, lt

  // Other names for the same wires on the sheet: t_pc0[32:0] = {idle0, pc0}; t_pc1[32:0] = {idle1, pc1};
  //   t_pc2[32:0] = {idle2, pc2}; t_pc3[32:0] = {idle3, pc3}
endmodule

module rvr32_id (
  input  [31:0] inst,
  output [23:0] uop,
  output [14:0] rsd,
  output type_s,
  output type_b,
  output type_u,
  output type_j,
  output wfs_glb,
  output br_f,
  output br_b,
  output jal,
  output jalr
);

  wire and_5_out, and_6_out, and_7_out, and_8_out, and_10_out, and_11_out, and_12_out, and_13_out,
       and_14_out, and_15_out, and_16_out, and_17_out, and_18_out, and_23_out, and_24_out, nor_1_out,
       or_1_out, or_2_out, or_4_out, or_7_out, or_8_out, or_9_out, xor_1_out, xor_2_out;

  and and_1 (type_s, ~inst[4], inst[5], ~inst[6]);  // AND_Gate
  and and_2 (type_u, inst[2], ~inst[3], inst[4]);  // AND_Gate
  and and_3 (type_j, inst[2], inst[3], ~inst[4], inst[5]);  // AND_Gate
  and and_4 (type_b, ~inst[2], ~inst[4], inst[5], inst[6]);  // AND_Gate
  and and_5 (and_5_out, ~inst[2], inst[4]);  // AND_Gate
  and and_6 (and_6_out, inst[2], inst[5], inst[4]);
  and and_7 (and_7_out, inst[6], inst[5], inst[4]);
  and and_8 (and_8_out, inst[30], ~inst[31]);  // AND_Gate
  or or_1 (or_1_out, inst[3], ~inst[5]);  // OR_Gate
  nand nand_1 (uop[16], or_1_out, inst[2]);
  or or_2 (or_2_out, inst[6], inst[4]);
  and and_9 (uop[17], or_2_out, ~inst[2], inst[5]);  // AND_Gate
  and and_10 (and_10_out, ~inst[13], inst[12]);  // AND_Gate
  and and_11 (and_11_out, inst[12], inst[14]);
  and and_12 (and_12_out, inst[14], inst[13]);
  and and_13 (and_13_out, inst[13], inst[12]);
  or or_3 (uop[6], inst[13], inst[14]);
  and and_14 (and_14_out, ~inst[13], inst[30], inst[12]);  // AND_Gate
  or or_4 (or_4_out, and_14_out, and_15_out);
  and and_15 (and_15_out, inst[30], inst[5]);
  and and_16 (and_16_out, inst[14], ~xor_1_out);  // AND_Gate
  xor xor_1 (xor_1_out, inst[12], inst[13]);
  xor xor_2 (xor_2_out, inst[13], inst[14]);
  and and_17 (and_17_out, ~inst[13], inst[12]);  // AND_Gate
  and and_18 (and_18_out, inst[14], ~inst[12]);  // AND_Gate
  and and_19 (uop[14], and_7_out, nor_1_out);
  nor nor_1 (nor_1_out, inst[14], inst[13], inst[12]);
  and and_20 (uop[15], and_7_out, and_8_out, inst[15]);
  and and_21 (wfs_glb, and_7_out, and_8_out, inst[17]);
  or or_5 (uop[4], and_10_out, and_11_out);
  or or_6 (uop[5], and_12_out, and_13_out);
  or or_7 (or_7_out, or_4_out, and_16_out);
  and and_22 (uop[12], or_7_out, and_5_out);
  nor nor_2 (uop[13], xor_2_out, inst[2]);
  or or_8 (or_8_out, and_17_out, inst[14]);
  and and_23 (and_23_out, or_8_out, and_5_out);
  or or_9 (or_9_out, inst[13], and_18_out);
  and and_24 (and_24_out, or_9_out, and_5_out);
  nand nand_2 (uop[20], ~inst[2], ~inst[4], inst[5]);  // NAND_Gate
  and and_25 (uop[21], ~inst[2], inst[4], inst[5], ~inst[6], inst[25]);  // AND_Gate
  and and_26 (uop[22], ~inst[2], ~inst[4], inst[5], inst[6]);  // AND_Gate
  and and_27 (uop[23], inst[2], ~inst[4], inst[5], inst[6]);  // AND_Gate
  or or_10 (uop[10], and_23_out, and_6_out);
  or or_11 (uop[11], and_24_out, and_6_out);
  // Probe on uop[6:4]
  // Probe on {inst[5], inst[14:12]}
  // Probe on uop[13:10]
  // Probe on {uop[23:20], inst[6], inst[4], uop[17:14]}
  and and_28 (jal, uop[23], inst[3]);
  and and_29 (jalr, uop[23], ~inst[3]);  // AND_Gate
  and and_30 (br_f, ~inst[31], uop[22]);  // AND_Gate
  and and_31 (br_b, inst[31], uop[22]);

  assign rsd = {inst[24:15], inst[11:7]};
  assign {uop[19:18], uop[9:7], uop[3:0]} = {inst[6], inst[4], inst[14:12], inst[5], inst[14:12]};

  // Other names for the same wires on the sheet: op[6:0] = inst[6:0]; op_2 = inst[2]; op_3 = inst[3];
  //   funct7[6:0] = inst[31:25]; funct7_0 = inst[25]; funct7_5 = inst[30]; funct7_6 = inst[31]; rd[4:0] = inst[11:7];
  //   rs1[4:0] = inst[19:15]; rs1_0 = inst[15]; rs1_2 = inst[17]; rs2[4:0] = inst[24:20]; ealuop[2:0] = inst[14:12];
  //   funct3[2:0] = inst[14:12]; lsuop[3:0] = {inst[5], inst[14:12]}; op_5 = inst[5]; cmpop[2:0] = uop[6:4];
  //   aluop[3:0] = uop[13:10]; spop[9:0] = {uop[23:20], inst[6], inst[4], uop[17:14]}; op_4 = inst[4]; op_6 = inst[6]
endmodule

module rvr32_cu (
  input  clk,
  input  [31:0] inst_data,
  input  rst_n,
  input  [29:0] cuid,
  input  inst_ready,
  input  start,
  input  [31:0] glb_rdata,
  input  glb_ready,
  input  [31:0] loc_rdata0,
  input  loc_ready0,
  input  [31:0] loc_rdata1,
  input  loc_ready1,
  input  [31:0] loc_rdata2,
  input  loc_ready2,
  input  sync_ready,
  input  [31:0] loc_rdata3,
  input  loc_ready3,
  output [31:0] loc_addr0,
  output glb_valid,
  output [31:0] loc_wdata0,
  output [3:0] loc_wstrb0,
  output loc_valid0,
  output [31:0] glb_addr,
  output [3:0] glb_wstrb,
  output [31:0] glb_wdata,
  output [31:0] loc_addr1,
  output [31:0] loc_wdata1,
  output [3:0] loc_wstrb1,
  output loc_valid1,
  output [31:0] loc_addr2,
  output [31:0] loc_wdata2,
  output wfi,
  output [3:0] loc_wstrb2,
  output loc_valid2,
  output wfs,
  output [31:0] loc_addr3,
  output [31:0] loc_wdata3,
  output [31:0] inst_addr,
  output [3:0] loc_wstrb3,
  output loc_valid3
);

  wire all_wait, and_1_out, and_2_out, and_3_out, and_4_out, and_5_out, and_6_out, and_7_out, and_8_out,
       and_17_out, and_18_out, and_22_out, and_23_out, and_24_out, and_25_out, and_26_out, and_27_out,
       and_28_out, and_29_out, and_30_out, and_31_out, and_32_out, br_b, br_f, brc0, brc1, brc2, brc3, clk_n,
       cu_exec, cu_work, exec0, exec1, exec2, exec3, glb_ready0, glb_ready1, glb_ready2, glb_ready3,
       glb_valid0, glb_valid1, glb_valid2, glb_valid3, idle0, idle1, idle2, idle3, jal, jalr, not_2_out,
       not_3_out, or_1_out, or_2_out, or_3_out, or_4_out, or_5_out, or_6_out, or_7_out, or_9_out, or_10_out,
       or_11_out, or_12_out, or_13_out, pca_ready, req_brj, req_mem, req_pca, sp_sync_ready, u_id_type_b,
       u_id_type_j, u_id_type_s, u_id_type_u, u_sp0_mem_valid, u_sp1_mem_valid, u_sp2_mem_valid,
       u_sp3_mem_valid, wfi0, wfi1, wfi2, wfi3, wfs0, wfs1, wfs2, wfs3, wfs_glb;
  wire [14:0] rsd;
  wire [23:0] uop;
  wire [31:0] glb_rdata0, imm, minpc, multiplexer_1_out, multiplexer_2_out, multiplexer_3_out,
       multiplexer_4_out, pc0, pc1, pc2, pc3, r_inst_q;

  not not_1 (clk_n, clk);
  Multiplexer #(.width(32)) multiplexer_1 (
    .in0(glb_rdata0), .in1(loc_rdata0), .out(multiplexer_1_out), .sel(loc_addr0[31]));
  and and_1 (and_1_out, loc_ready0, loc_addr0[31]);
  and and_2 (and_2_out, glb_ready0, ~loc_addr0[31]);  // AND_Gate
  Multiplexer #(.width(32)) multiplexer_2 (
    .in0(glb_rdata0), .in1(loc_rdata1), .out(multiplexer_2_out), .sel(loc_addr1[31]));
  and and_3 (and_3_out, loc_ready1, loc_addr1[31]);
  and and_4 (and_4_out, glb_ready1, ~loc_addr1[31]);  // AND_Gate
  Multiplexer #(.width(32)) multiplexer_3 (
    .in0(glb_rdata0), .in1(loc_rdata2), .out(multiplexer_3_out), .sel(loc_addr2[31]));
  and and_5 (and_5_out, loc_ready2, loc_addr2[31]);
  and and_6 (and_6_out, glb_ready2, ~loc_addr2[31]);  // AND_Gate
  Multiplexer #(.width(32)) multiplexer_4 (
    .in0(glb_rdata0), .in1(loc_rdata3), .out(multiplexer_4_out), .sel(loc_addr3[31]));
  and and_7 (and_7_out, loc_ready3, loc_addr3[31]);
  and and_8 (and_8_out, glb_ready3, ~loc_addr3[31]);  // AND_Gate
  or or_1 (or_1_out, and_1_out, and_2_out);
  or or_2 (or_2_out, and_3_out, and_4_out);
  or or_3 (or_3_out, and_5_out, and_6_out);
  or or_4 (or_4_out, and_7_out, and_8_out);
  rvr32_sp u_sp0 (
    .rst_n(rst_n), .clk(clk_n), .spid({cuid, 2'b00}), .imm(imm), .sp_uop(uop), .rsd(rsd), .start(start),
    .inst_ready(inst_ready), .sync_ready(sp_sync_ready), .shared_pc(inst_addr),
    .mem_rdata(multiplexer_1_out), .mem_ready(or_1_out), .mem_wstrb(loc_wstrb0), .mem_valid(u_sp0_mem_valid),
    .mem_addr(loc_addr0), .mem_wdata(loc_wdata0), .brc(brc0), .pc(pc0), .wfs(wfs0), .wfi(wfi0), .exec(exec0));
  rvr32_sp u_sp1 (
    .rst_n(rst_n), .clk(clk_n), .spid({cuid, 2'b01}), .imm(imm), .sp_uop(uop), .rsd(rsd), .start(start),
    .inst_ready(inst_ready), .sync_ready(sp_sync_ready), .shared_pc(inst_addr),
    .mem_rdata(multiplexer_2_out), .mem_ready(or_2_out), .mem_wstrb(loc_wstrb1), .mem_valid(u_sp1_mem_valid),
    .mem_addr(loc_addr1), .mem_wdata(loc_wdata1), .brc(brc1), .pc(pc1), .wfs(wfs1), .wfi(wfi1), .exec(exec1));
  rvr32_sp u_sp2 (
    .rst_n(rst_n), .clk(clk_n), .spid({cuid, 2'b10}), .imm(imm), .sp_uop(uop), .rsd(rsd), .start(start),
    .inst_ready(inst_ready), .sync_ready(sp_sync_ready), .shared_pc(inst_addr),
    .mem_rdata(multiplexer_3_out), .mem_ready(or_3_out), .mem_wstrb(loc_wstrb2), .mem_valid(u_sp2_mem_valid),
    .mem_addr(loc_addr2), .mem_wdata(loc_wdata2), .brc(brc2), .pc(pc2), .wfs(wfs2), .wfi(wfi2), .exec(exec2));
  rvr32_sp u_sp3 (
    .rst_n(rst_n), .clk(clk_n), .spid({cuid, 2'b11}), .imm(imm), .sp_uop(uop), .rsd(rsd), .start(start),
    .inst_ready(inst_ready), .sync_ready(sp_sync_ready), .shared_pc(inst_addr),
    .mem_rdata(multiplexer_4_out), .mem_ready(or_4_out), .mem_wstrb(loc_wstrb3), .mem_valid(u_sp3_mem_valid),
    .mem_addr(loc_addr3), .mem_wdata(loc_wdata3), .brc(brc3), .pc(pc3), .wfs(wfs3), .wfi(wfi3), .exec(exec3));
  nor nor_1 (all_wait, exec0, exec1, exec2, exec3);
  and and_9 (loc_valid0, u_sp0_mem_valid, loc_addr0[31]);
  and and_10 (glb_valid0, u_sp0_mem_valid, ~loc_addr0[31]);  // AND_Gate
  and and_11 (loc_valid1, u_sp1_mem_valid, loc_addr1[31]);
  and and_12 (glb_valid1, u_sp1_mem_valid, ~loc_addr1[31]);  // AND_Gate
  and and_13 (loc_valid2, u_sp2_mem_valid, loc_addr2[31]);
  and and_14 (glb_valid2, u_sp2_mem_valid, ~loc_addr2[31]);  // AND_Gate
  and and_15 (loc_valid3, u_sp3_mem_valid, loc_addr3[31]);
  and and_16 (glb_valid3, u_sp3_mem_valid, ~loc_addr3[31]);  // AND_Gate
  or or_5 (or_5_out, ~req_mem, all_wait);  // OR_Gate
  or or_6 (or_6_out, ~req_pca, pca_ready);  // OR_Gate
  and and_17 (and_17_out, cu_exec, or_5_out, or_6_out);
  and and_18 (and_18_out, inst_ready, cu_work);
  Register #(.width(32)) r_inst (.D(inst_data), .en(inst_ready), .clk(clk), .Q(r_inst_q), .clr(not_2_out));
  not not_2 (not_2_out, rst_n);
  Register #(.width(1)) r_cu_exec (.D(and_18_out), .en(1'b1), .clk(clk), .Q(cu_exec), .clr(not_3_out));
  not not_3 (not_3_out, rst_n);
  and and_19 (wfs, wfs0, wfs1, wfs2, wfs3);
  and and_20 (wfi, wfi0, wfi1, wfi2, wfi3);
  not not_4 (cu_work, wfi);
  or or_7 (or_7_out, ~wfs_glb, sync_ready);  // OR_Gate
  rvr32_sharedpc u_shared_pc (
    .we(and_17_out), .clk(clk_n), .rst_n(cu_work), .jdata(minpc), .jmp(req_pca), .bjimm(imm), .brj(req_brj),
    .pc(inst_addr));
  rvr32_lsa_4p u_lsa (
    .mem_rdata(glb_rdata), .mem_ready(glb_ready), .addr0(loc_addr0), .addr1(loc_addr1), .addr2(loc_addr2),
    .addr3(loc_addr3), .wstrb0(loc_wstrb0), .wstrb1(loc_wstrb1), .wstrb2(loc_wstrb2), .wstrb3(loc_wstrb3),
    .wdata0(loc_wdata0), .wdata1(loc_wdata1), .wdata2(loc_wdata2), .wdata3(loc_wdata3), .valid0(glb_valid0),
    .clk(clk), .valid1(glb_valid1), .valid2(glb_valid2), .valid3(glb_valid3), .rst_n(rst_n),
    .rdata(glb_rdata0), .mem_valid(glb_valid), .ready0(glb_ready0), .ready1(glb_ready1), .ready2(glb_ready2),
    .ready3(glb_ready3), .mem_addr(glb_addr), .mem_wstrb(glb_wstrb), .mem_wdata(glb_wdata));
  and and_21 (sp_sync_ready, wfs, or_7_out);
  rvr32_id u_id (
    .inst(r_inst_q), .uop(uop), .rsd(rsd), .type_s(u_id_type_s), .type_b(u_id_type_b), .type_u(u_id_type_u),
    .type_j(u_id_type_j), .wfs_glb(wfs_glb), .br_f(br_f), .br_b(br_b), .jal(jal), .jalr(jalr));
  or or_8 (req_pca, jalr, uop[14], uop[15]);
  nor nor_2 (req_mem, uop[18], uop[19]);
  and and_22 (and_22_out, exec0, brc0);
  or or_9 (or_9_out, ~exec0, brc0);  // OR_Gate
  and and_23 (and_23_out, exec1, brc1);
  or or_10 (or_10_out, ~exec1, brc1);  // OR_Gate
  and and_24 (and_24_out, exec2, brc2);
  or or_11 (or_11_out, ~exec2, brc2);  // OR_Gate
  and and_25 (and_25_out, exec3, brc3);
  or or_12 (or_12_out, ~exec3, brc3);  // OR_Gate
  and and_26 (and_26_out, br_b, or_13_out);
  or or_13 (or_13_out, and_22_out, and_23_out, and_24_out, and_25_out);
  and and_27 (and_27_out, or_9_out, or_10_out, or_11_out, or_12_out);
  and and_28 (and_28_out, and_27_out, br_f);
  rvr32_pca_4p u_pca (
    .idle0(idle0), .idle1(idle1), .idle2(idle2), .idle3(idle3), .pc0(pc0), .pc1(pc1), .pc2(pc2), .pc3(pc3),
    .req(req_pca), .clk(clk_n), .rst_n(cu_exec), .min_pc(minpc), .ready(pca_ready));
  or or_14 (req_brj, and_26_out, jal, and_28_out);
  rvr32_immgen u_immgen (
    .data_inst(r_inst_q), .type_b(u_id_type_b), .type_s(u_id_type_s), .type_u(u_id_type_u),
    .type_j(u_id_type_j), .data_out(imm));
  or or_15 (idle0, wfi0, wfs0, and_29_out);
  and and_29 (and_29_out, jalr, ~exec0);  // AND_Gate
  or or_16 (idle1, wfi1, wfs1, and_30_out);
  and and_30 (and_30_out, jalr, ~exec1);  // AND_Gate
  or or_17 (idle2, wfi2, wfs2, and_31_out);
  and and_31 (and_31_out, jalr, ~exec2);  // AND_Gate
  or or_18 (idle3, wfi3, wfs3, and_32_out);
  and and_32 (and_32_out, jalr, ~exec3);  // AND_Gate

  // Other names for the same wires on the sheet: glb_addr0[31:0] = loc_addr0; addr0_31 = loc_addr0[31];
  //   glb_addr1[31:0] = loc_addr1; addr1_31 = loc_addr1[31]; glb_addr2[31:0] = loc_addr2; addr2_31 = loc_addr2[31];
  //   glb_addr3[31:0] = loc_addr3; addr3_31 = loc_addr3[31]; glb_rdata1[31:0] = glb_rdata0;
  //   glb_rdata2[31:0] = glb_rdata0; glb_rdata3[31:0] = glb_rdata0; glb_wdata0[31:0] = loc_wdata0;
  //   glb_wdata1[31:0] = loc_wdata1; glb_wdata2[31:0] = loc_wdata2; glb_wdata3[31:0] = loc_wdata3;
  //   glb_wstrb0[3:0] = loc_wstrb0; glb_wstrb1[3:0] = loc_wstrb1; glb_wstrb2[3:0] = loc_wstrb2;
  //   glb_wstrb3[3:0] = loc_wstrb3; sharedpc[31:0] = inst_addr; sp_inst_ready = inst_ready; sp_rst_n = rst_n;
  //   sp_start = start; wfi_sp = uop[14]; wfs_cu = uop[15]
endmodule

module rvr32_mc (
  input  [31:0] addr,
  input  [31:0] wdata,
  input  [3:0] wstrb,
  input  [31:0] mem_rdata,
  input  clk,
  input  valid,
  input  clk_mem,
  output [31:0] mem_addr,
  output [31:0] mem_wdata,
  output [31:0] rdata,
  output ready,
  output mem_we,
  output mem_ce
);

  wire and_1_out, and_2_out, and_3_out, and_4_out, and_6_out, mem_ready, not_1_out, not_2_out, not_3_out,
       not_4_out, not_5_out, r_valid0_q, shb, we, whb0, whb1, xnor_1_out;
  wire [31:0] r_data_q;

  and and_1 (and_1_out, mem_ready, shb);
  and and_2 (and_2_out, valid, xnor_1_out);
  not not_1 (not_1_out, whb0);
  Register #(.width(1)) r_whb0 (.D(not_1_out), .en(and_1_out), .clk(clk), .Q(whb0), .clr(not_2_out));
  not not_2 (not_2_out, valid);
  Register #(.width(1)) r_valid0 (.D(1'b1), .en(1'b1), .clk(clk_mem), .Q(r_valid0_q), .clr(not_3_out));
  not not_3 (not_3_out, and_2_out);
  and and_3 (and_3_out, ~whb1, shb);  // AND_Gate
  Register #(.width(1)) r_whb1 (.D(whb0), .en(1'b1), .clk(not_4_out), .Q(whb1), .clr(not_2_out));
  not not_4 (not_4_out, clk);
  Register #(.width(1)) r_valid1 (.D(r_valid0_q), .en(1'b1), .clk(clk_mem), .Q(mem_ready), .clr(not_3_out));
  or or_1 (we, wstrb[3], wstrb[2], wstrb[1], wstrb[0]);
  and and_4 (and_4_out, wstrb[3], wstrb[2], wstrb[1], wstrb[0]);
  Register #(.width(32)) r_data (.D(mem_rdata), .en(and_3_out), .clk(clk), .Q(r_data_q), .clr(not_5_out));
  not not_5 (not_5_out, valid);
  and and_5 (shb, we, ~and_4_out);  // AND_Gate
  and and_6 (and_6_out, mem_ready, whb0, whb1);
  xnor xnor_1 (xnor_1_out, whb1, whb0);
  Multiplexer #(.width(8)) multiplexer_1 (.in0(r_data_q[7:0]), .in1(wdata[7:0]), .out(mem_wdata[7:0]), .sel(wstrb[0]));
  Multiplexer #(.width(8)) multiplexer_2 (
    .in0(r_data_q[15:8]), .in1(wdata[15:8]), .out(mem_wdata[15:8]), .sel(wstrb[1]));
  Multiplexer #(.width(8)) multiplexer_3 (
    .in0(r_data_q[23:16]), .in1(wdata[23:16]), .out(mem_wdata[23:16]), .sel(wstrb[2]));
  Multiplexer #(.width(8)) multiplexer_4 (
    .in0(r_data_q[31:24]), .in1(wdata[31:24]), .out(mem_wdata[31:24]), .sel(wstrb[3]));
  Multiplexer multiplexer_5 (.in0(mem_ready), .in1(and_6_out), .out(ready), .sel(shb));
  Multiplexer multiplexer_6 (.in0(we), .in1(whb0), .out(mem_we), .sel(shb));

  assign mem_addr = addr;
  assign mem_ce = valid;
  assign rdata = mem_rdata;
endmodule

module rvr32_core (
  input  clk_2x,
  input  clk_1x,
  input  [31:0] inst_data,
  input  rst_n,
  input  [29:0] cuid,
  input  inst_ready,
  input  start,
  input  [31:0] glb_rdata,
  input  glb_ready,
  input  sync_ready,
  output glb_valid,
  output [31:0] glb_addr,
  output [3:0] glb_wstrb,
  output [31:0] glb_wdata,
  output wfi,
  output wfs,
  output [31:0] inst_addr
);

  wire and_1_out, and_2_out, and_3_out, and_4_out, and_5_out, and_6_out, and_7_out, and_8_out, clk_mem,
       clk_n, loc_ready0, loc_ready1, loc_ready2, loc_ready3, loc_valid0, loc_valid1, loc_valid2, loc_valid3,
       not_3_out, not_4_out, not_5_out, not_6_out, rvr32_mc_1_mem_ce, rvr32_mc_1_mem_we, u_mc0_mem_ce,
       u_mc0_mem_we, u_mc1_mem_ce, u_mc1_mem_we, u_mc2_mem_ce, u_mc2_mem_we;
  wire [3:0] loc_wstrb0, loc_wstrb1, loc_wstrb2, loc_wstrb3;
  wire [31:0] loc_addr0, loc_addr1, loc_addr2, loc_addr3, loc_rdata0, loc_rdata1, loc_rdata2, loc_rdata3,
       loc_wdata0, loc_wdata1, loc_wdata2, loc_wdata3, ram_1_dout, rvr32_mc_1_mem_addr, rvr32_mc_1_mem_wdata,
       u_locram0_dout, u_locram1_dout, u_locram2_dout, u_mc0_mem_addr, u_mc0_mem_wdata, u_mc1_mem_addr,
       u_mc1_mem_wdata, u_mc2_mem_addr, u_mc2_mem_wdata;

  not not_1 (clk_n, clk_1x);
  not not_2 (clk_mem, clk_2x);
  rvr32_mc u_mc0 (
    .addr(loc_addr0), .wdata(loc_wdata0), .wstrb(loc_wstrb0), .mem_rdata(u_locram0_dout), .clk(clk_n),
    .valid(loc_valid0), .clk_mem(clk_mem), .mem_addr(u_mc0_mem_addr), .mem_wdata(u_mc0_mem_wdata),
    .rdata(loc_rdata0), .ready(loc_ready0), .mem_we(u_mc0_mem_we), .mem_ce(u_mc0_mem_ce));
  rvr32_cu u_cu (
    .inst_ready(inst_ready), .start(start), .rst_n(rst_n), .cuid(cuid), .clk(clk_1x), .glb_rdata(glb_rdata),
    .glb_ready(glb_ready), .sync_ready(sync_ready), .loc_rdata2(loc_rdata2), .loc_ready2(loc_ready2),
    .loc_rdata3(loc_rdata3), .loc_ready3(loc_ready3), .loc_rdata0(loc_rdata0), .loc_ready0(loc_ready0),
    .loc_rdata1(loc_rdata1), .loc_ready1(loc_ready1), .inst_data(inst_data), .loc_addr2(loc_addr2),
    .loc_addr3(loc_addr3), .loc_addr0(loc_addr0), .loc_addr1(loc_addr1), .loc_valid2(loc_valid2),
    .loc_valid3(loc_valid3), .loc_valid0(loc_valid0), .loc_valid1(loc_valid1), .loc_wdata2(loc_wdata2),
    .loc_wdata3(loc_wdata3), .loc_wdata0(loc_wdata0), .loc_wdata1(loc_wdata1), .loc_wstrb2(loc_wstrb2),
    .loc_wstrb3(loc_wstrb3), .loc_wstrb0(loc_wstrb0), .loc_wstrb1(loc_wstrb1), .inst_addr(inst_addr),
    .wfs(wfs), .wfi(wfi), .glb_wdata(glb_wdata), .glb_wstrb(glb_wstrb), .glb_addr(glb_addr),
    .glb_valid(glb_valid));
  and and_1 (and_1_out, u_mc0_mem_we, u_mc0_mem_ce);
  and and_2 (and_2_out, ~u_mc0_mem_we, u_mc0_mem_ce);  // AND_Gate
  not not_3 (not_3_out, clk_2x);
  RAM #(.addrWidth(10), .dataWidth(32)) u_locram0 (
    .addr(u_mc0_mem_addr[11:2]), .we(and_1_out), .oe(and_2_out), .clk(not_3_out), .din(u_mc0_mem_wdata),
    .dout(u_locram0_dout));
  rvr32_mc u_mc1 (
    .addr(loc_addr1), .wdata(loc_wdata1), .wstrb(loc_wstrb1), .mem_rdata(u_locram1_dout), .clk(clk_n),
    .valid(loc_valid1), .clk_mem(clk_mem), .mem_addr(u_mc1_mem_addr), .mem_wdata(u_mc1_mem_wdata),
    .rdata(loc_rdata1), .ready(loc_ready1), .mem_we(u_mc1_mem_we), .mem_ce(u_mc1_mem_ce));
  and and_3 (and_3_out, u_mc1_mem_we, u_mc1_mem_ce);
  and and_4 (and_4_out, ~u_mc1_mem_we, u_mc1_mem_ce);  // AND_Gate
  not not_4 (not_4_out, clk_2x);
  RAM #(.addrWidth(10), .dataWidth(32)) u_locram1 (
    .addr(u_mc1_mem_addr[11:2]), .we(and_3_out), .oe(and_4_out), .clk(not_4_out), .din(u_mc1_mem_wdata),
    .dout(u_locram1_dout));
  rvr32_mc u_mc2 (
    .addr(loc_addr2), .wdata(loc_wdata2), .wstrb(loc_wstrb2), .mem_rdata(u_locram2_dout), .clk(clk_n),
    .valid(loc_valid2), .clk_mem(clk_mem), .mem_addr(u_mc2_mem_addr), .mem_wdata(u_mc2_mem_wdata),
    .rdata(loc_rdata2), .ready(loc_ready2), .mem_we(u_mc2_mem_we), .mem_ce(u_mc2_mem_ce));
  not not_5 (not_5_out, clk_2x);
  and and_5 (and_5_out, u_mc2_mem_we, u_mc2_mem_ce);
  and and_6 (and_6_out, ~u_mc2_mem_we, u_mc2_mem_ce);  // AND_Gate
  RAM #(.addrWidth(10), .dataWidth(32)) u_locram2 (
    .addr(u_mc2_mem_addr[11:2]), .we(and_5_out), .oe(and_6_out), .clk(not_5_out), .din(u_mc2_mem_wdata),
    .dout(u_locram2_dout));
  rvr32_mc rvr32_mc_1 (
    .addr(loc_addr3), .wdata(loc_wdata3), .wstrb(loc_wstrb3), .mem_rdata(ram_1_dout), .clk(clk_n),
    .valid(loc_valid3), .clk_mem(clk_mem), .mem_addr(rvr32_mc_1_mem_addr), .mem_wdata(rvr32_mc_1_mem_wdata),
    .rdata(loc_rdata3), .ready(loc_ready3), .mem_we(rvr32_mc_1_mem_we), .mem_ce(rvr32_mc_1_mem_ce));
  and and_7 (and_7_out, rvr32_mc_1_mem_we, rvr32_mc_1_mem_ce);
  and and_8 (and_8_out, ~rvr32_mc_1_mem_we, rvr32_mc_1_mem_ce);  // AND_Gate
  not not_6 (not_6_out, clk_2x);
  RAM #(.addrWidth(10), .dataWidth(32)) ram_1 (
    .addr(rvr32_mc_1_mem_addr[11:2]), .we(and_7_out), .oe(and_8_out), .clk(not_6_out),
    .din(rvr32_mc_1_mem_wdata), .dout(ram_1_dout));

  // Other names for the same wires on the sheet: clk = clk_1x
endmodule

module rvr32_rover (
  input  start,
  input  clk,
  input  rst_n,
  input  [31:0] irom_data0,
  input  [31:0] irom_data1,
  input  [31:0] dram_rdata,
  output dram_clk,
  output wfi,
  output [31:0] irom_addr0,
  output [31:0] irom_addr1,
  output [31:0] dram_addr,
  output [31:0] dram_wdata,
  output dram_we,
  output dram_ce
);

  wire clk_1x, clk_1x_n, not_3_out, u_core0_glb_valid, u_core0_wfi, u_core0_wfs, u_core1_glb_valid,
       u_core1_wfi, u_core1_wfs, u_glblsa_mem_valid, u_glblsa_ready0, u_glblsa_ready1, u_glbmc_ready;
  wire [3:0] u_core0_glb_wstrb, u_core1_glb_wstrb, u_glblsa_mem_wstrb;
  wire [31:0] u_core0_glb_addr, u_core0_glb_wdata, u_core1_glb_addr, u_core1_glb_wdata, u_glblsa_mem_addr,
       u_glblsa_mem_wdata, u_glblsa_rdata, u_glbmc_rdata;

  not not_1 (dram_clk, clk);
  rvr32_core u_core0 (
    .clk_2x(clk), .clk_1x(clk_1x), .inst_data(irom_data0), .rst_n(rst_n), .cuid({30{1'b0}}),
    .inst_ready(1'b1), .start(start), .glb_rdata(u_glblsa_rdata), .glb_ready(u_glblsa_ready0),
    .sync_ready(u_core1_wfs), .glb_valid(u_core0_glb_valid), .glb_addr(u_core0_glb_addr),
    .glb_wstrb(u_core0_glb_wstrb), .glb_wdata(u_core0_glb_wdata), .wfi(u_core0_wfi), .wfs(u_core0_wfs),
    .inst_addr(irom_addr0));
  not not_2 (clk_1x_n, clk_1x);
  Register #(.width(1)) register_1 (.D(clk_1x_n), .en(1'b1), .clk(clk), .Q(clk_1x), .clr(not_3_out));
  not not_3 (not_3_out, rst_n);
  and and_1 (wfi, u_core0_wfi, u_core1_wfi);
  rvr32_lsa_2p u_glblsa (
    .mem_rdata(u_glbmc_rdata), .valid0(u_core0_glb_valid), .addr0(u_core0_glb_addr),
    .addr1(u_core1_glb_addr), .valid1(u_core1_glb_valid), .wstrb0(u_core0_glb_wstrb),
    .wstrb1(u_core1_glb_wstrb), .clk(clk_1x), .wdata0(u_core0_glb_wdata), .wdata1(u_core1_glb_wdata),
    .rst_n(rst_n), .mem_ready(u_glbmc_ready), .rdata(u_glblsa_rdata), .mem_addr(u_glblsa_mem_addr),
    .mem_valid(u_glblsa_mem_valid), .mem_wstrb(u_glblsa_mem_wstrb), .mem_wdata(u_glblsa_mem_wdata),
    .ready0(u_glblsa_ready0), .ready1(u_glblsa_ready1));
  rvr32_mc u_glbmc (
    .addr(u_glblsa_mem_addr), .wdata(u_glblsa_mem_wdata), .wstrb(u_glblsa_mem_wstrb), .mem_rdata(dram_rdata),
    .clk(clk_1x_n), .valid(u_glblsa_mem_valid), .clk_mem(dram_clk), .mem_addr(dram_addr),
    .mem_wdata(dram_wdata), .rdata(u_glbmc_rdata), .ready(u_glbmc_ready), .mem_we(dram_we), .mem_ce(dram_ce));
  rvr32_core u_core1 (
    .clk_2x(clk), .clk_1x(clk_1x), .inst_data(irom_data1), .rst_n(rst_n), .cuid(30'h1), .inst_ready(1'b1),
    .start(start), .glb_rdata(u_glblsa_rdata), .glb_ready(u_glblsa_ready1), .sync_ready(u_core0_wfs),
    .glb_valid(u_core1_glb_valid), .glb_addr(u_core1_glb_addr), .glb_wstrb(u_core1_glb_wstrb),
    .glb_wdata(u_core1_glb_wdata), .wfi(u_core1_wfi), .wfs(u_core1_wfs), .inst_addr(irom_addr1));

  // Other names for the same wires on the sheet: clk_2x = clk; clk_2x_n = dram_clk
endmodule

module main (
  input  start,
  input  rst_n,
  input  clear0,
  input  clear1,
  input  clearm
);

  wire and_3_out, and_4_out, and_6_out, clock_1_out, mclk, oe, rgb_video_1_p3, sel0, sel1, sel2, sel3,
       u_gpu_dram_ce, u_gpu_dram_we, u_gpu_wfi, we;
  wire [13:0] addr;
  wire [31:0] multiplexer_1_out, rdata0, rdata1, u_gpu_dram_addr, u_gpu_irom_addr0, u_gpu_irom_addr1,
       u_rom0_data, u_rom1_data, wdata;

  ROM #(.addrWidth(16), .dataWidth(32)) u_rom0 (.addr(u_gpu_irom_addr0[17:2]), .data(u_rom0_data));
  Clock clock_1 (.out(clock_1_out));
  // Probe on u_gpu_wfi
  ROM #(.addrWidth(16), .dataWidth(32)) u_rom1 (.addr(u_gpu_irom_addr1[17:2]), .data(u_rom1_data));
  Decoder #(.enable("false"), .select(2)) decoder_1 (
    .out0(sel0), .out1(sel1), .out2(sel2), .out3(sel3), .sel(u_gpu_dram_addr[17:16]));
  rvr32_rover u_gpu (
    .irom_data1(u_rom1_data), .rst_n(rst_n), .start(start), .clk(clock_1_out), .irom_data0(u_rom0_data),
    .dram_rdata(multiplexer_1_out), .irom_addr0(u_gpu_irom_addr0), .wfi(u_gpu_wfi),
    .dram_addr({u_gpu_dram_addr[31:16], addr, u_gpu_dram_addr[1:0]}), .dram_wdata(wdata),
    .dram_we(u_gpu_dram_we), .dram_ce(u_gpu_dram_ce), .irom_addr1(u_gpu_irom_addr1), .dram_clk(mclk));
  and and_1 (we, u_gpu_dram_we, u_gpu_dram_ce);
  and and_2 (oe, u_gpu_dram_ce, ~u_gpu_dram_we);  // AND_Gate
  Multiplexer #(.width(32)) multiplexer_1 (.in0(rdata0), .in1(rdata1), .out(multiplexer_1_out), .sel(sel1));
  and and_3 (and_3_out, we, sel0);
  and and_4 (and_4_out, sel0, oe);
  // RGB_Video #(.cursor("No Cursor")) rgb_video_1: pin names not known; wires that end beside it: clear0, mclk, rgb_video_1_p3, addr[6:0], addr[13:7], wdata[23:0]
  and and_5 (rgb_video_1_p3, we, sel2);
  and and_6 (and_6_out, we, sel3);
  RAM #(.addrWidth(14), .clearpin("true"), .dataWidth(32)) u_glbram (
    .addr(addr), .we(and_3_out), .oe(and_4_out), .clk(mclk), .din(wdata), .dout(rdata0), .clr(clearm));
  ROM #(.addrWidth(14), .dataWidth(32)) u_glbrom (.addr(addr), .data(rdata1));
  // RGB_Video #(.cursor("No Cursor"), .height(64), .scale(4)) rgb_video_2: pin names not known; wires that end beside it: clear1, mclk, and_6_out, addr[12:6], addr[5:0], wdata[15:0]

  // Notes on the sheet:
  //   contents of u_rom0 (hex, n*v repeats v):
  //   197 80018193 113 10010417 ff440413 10010497 fec48493 fffff917 fe490913 945c63 42283 592023 440413
  //   490913 fedff06f fffff417 fc440413 fffff497 fbc48493 945863 42023 440413 ff5ff06f 10010417 fa440413
  //   10010497 f9c48493 945a63 42903 900e7 440413 ff1ff06f 20c000ef 10500073 52683 452703 852783 41f6d313
  //   b6d613 41f75893 41f7d813 1531313 666333 a75593 b7d613 1689893 1581813 8e37 fffe0e13 115e8b3 1066833
  //   41f35513 1c57533 41f8d593 41f85613 1569693 1c5f5b3 1c67633 d506b3 1671713 1579793 e58733 f607b3
  //   a6b533 650533 b735b3 c7b633 1060633 11585b3 1151813 f6d693 41f55f93 d866b3 1f55293 1159893 1161813
  //   f75713 f7d793 41f5de93 41f65e13 d283b3 1f5df13 1f65313 e8e733 f867b3 1f6c6b3 f30833 ef08b3 40f55513
  //   53b2b3 41f686b3 1d74733 1c7c7b3 a282b3 40f5d593 40f65613 683333 16f693 1e8bf33 41d70733 41c787b3
  //   bf0f33 c30333 1f29293 13d513 1f6c6b3 177713 17f793 a2e533 185613 41f686b3 1ff1f13 18d593 1d74733
  //   1f31313 1c7c7b3 bf65b3 41d70733 c36633 41c787b3 d506b3 ffff0837 e585b3 f60633 513 d85a63 10537
  //   2007b7 80050513 6f6c663 ffff07b7 b7d863 4007b7 2f5ce63 7e050513 ffff07b7 2c7d663 2007b7 f64663
  //   1f50513 8067 41f65793 1079793 107d793 c787b3 4107d793 f50533 8067 41f5d793 1079793 107d793 b787b3
  //   4107d793 579793 f50533 fb1ff06f 41f6d513 1051513 1055513 d50533 41055513 b51513 f81ff06f fa010113
  //   4112e23 4812c23 4912a23 5212823 5312623 5412423 5512223 5612023 3712e23 3812c23 3912a23 3a12823
  //   3b12623 f1402c73 4007b7 30078793 fc07b3 879793 1937 89b7 f12623 f078d13 4f00493 fff98993 80090913
  //   10a37 c12b03 a93 b93 1184c263 10b9413 10ad793 f46433 b0c93 c0d93 10d9793 41f7d813 1f7d893 11d9713
  //   181593 f70533 b8e5b3 10585b3 e53733 b70733 271713 251593 1e55513 f587b3 e56733 1070733 b7b5b3 e585b3
  //   1a7d813 679513 659713 40f507b3 e86733 f53533 40b70733 40a705b3 41f5d713 1377733 f707b3 e7b733 b70733
  //   1171593 f7d793 41f75813 1f75513 f5e7b3 f505b3 107c7b3 a5b533 410787b3 40f75713 e50533 17f793 15d713
  //   107c7b3 1f51513 410787b3 e56733 f70733 1410513 e12a23 812c23 1412e23 c99ff0ef aca023 7c00d073 8d8d93
  //   12c8cb3 f1b4dce3 44407b7 fa87b3 157b733 4b0b13 78a93 1770bb3 ef6d12e3 ed5ff06f
  //   contents of u_rom1 (hex, n*v repeats v):
  //   197 80018193 113 10010417 ff440413 10010497 fec48493 fffff917 fe490913 945c63 42283 592023 440413
  //   490913 fedff06f fffff417 fc440413 fffff497 fbc48493 945863 42023 440413 ff5ff06f 10010417 fa440413
  //   10010497 f9c48493 945a63 42903 900e7 440413 ff1ff06f 20c000ef 10500073 52683 452703 852783 41f6d313
  //   b6d613 41f75893 41f7d813 1531313 666333 a75593 b7d613 1689893 1581813 8e37 fffe0e13 115e8b3 1066833
  //   41f35513 1c57533 41f8d593 41f85613 1569693 1c5f5b3 1c67633 d506b3 1671713 1579793 e58733 f607b3
  //   a6b533 650533 b735b3 c7b633 1060633 11585b3 1151813 f6d693 41f55f93 d866b3 1f55293 1159893 1161813
  //   f75713 f7d793 41f5de93 41f65e13 d283b3 1f5df13 1f65313 e8e733 f867b3 1f6c6b3 f30833 ef08b3 40f55513
  //   53b2b3 41f686b3 1d74733 1c7c7b3 a282b3 40f5d593 40f65613 683333 16f693 1e8bf33 41d70733 41c787b3
  //   bf0f33 c30333 1f29293 13d513 1f6c6b3 177713 17f793 a2e533 185613 41f686b3 1ff1f13 18d593 1d74733
  //   1f31313 1c7c7b3 bf65b3 41d70733 c36633 41c787b3 d506b3 ffff0837 e585b3 f60633 513 d85a63 10537
  //   2007b7 80050513 6f6c663 ffff07b7 b7d863 4007b7 2f5ce63 7e050513 ffff07b7 2c7d663 2007b7 f64663
  //   1f50513 8067 41f65793 1079793 107d793 c787b3 4107d793 f50533 8067 41f5d793 1079793 107d793 b787b3
  //   4107d793 579793 f50533 fb1ff06f 41f6d513 1051513 1055513 d50533 41055513 b51513 f81ff06f fa010113
  //   4112e23 4812c23 4912a23 5212823 5312623 5412423 5512223 5612023 3712e23 3812c23 3912a23 3a12823
  //   3b12623 f1402c73 4007b7 30078793 fc07b3 879793 1937 89b7 f12623 f078d13 4f00493 fff98993 80090913
  //   10a37 c12b03 a93 b93 1184c263 10b9413 10ad793 f46433 b0c93 c0d93 10d9793 41f7d813 1f7d893 11d9713
  //   181593 f70533 b8e5b3 10585b3 e53733 b70733 271713 251593 1e55513 f587b3 e56733 1070733 b7b5b3 e585b3
  //   1a7d813 679513 659713 40f507b3 e86733 f53533 40b70733 40a705b3 41f5d713 1377733 f707b3 e7b733 b70733
  //   1171593 f7d793 41f75813 1f75513 f5e7b3 f505b3 107c7b3 a5b533 410787b3 40f75713 e50533 17f793 15d713
  //   107c7b3 1f51513 410787b3 e56733 f70733 1410513 e12a23 812c23 1412e23 c99ff0ef aca023 7c00d073 8d8d93
  //   12c8cb3 f1b4dce3 44407b7 fa87b3 157b733 4b0b13 78a93 1770bb3 ef6d12e3 ed5ff06f
  //   contents of u_glbrom (hex, n*v repeats v):
  //   2020100 3030303 4040404 4040404 4*5050505 8*6060606 16*7070707 32*8080808
endmodule

module test (
  input  [31:0] rdata,
  input  clk_2x,
  input  [31:0] in_3,
  input  [3:0] in_4,
  input  req,
  input  rst_n,
  input  enable
);

  wire digital_oscilloscope_1_p3, digital_oscilloscope_1_p4, digital_oscilloscope_1_p5,
       digital_oscilloscope_1_p6, digital_oscilloscope_1_p8, not_1_out, not_2_out, not_3_out, not_4_out,
       register_1_q;
  wire [3:0] rvr32_lsu_1_mem_wstrb;
  wire [31:0] rvr32_lsu_1_rdata, rvr32_mc_1_mem_wdata, rvr32_mc_1_rdata;

  not not_1 (not_1_out, clk_2x);
  not not_2 (not_2_out, register_1_q);
  Register #(.width(1)) register_1 (.D(not_2_out), .en(1'b1), .clk(clk_2x), .Q(register_1_q), .clr(not_3_out));
  not not_3 (not_3_out, rst_n);
  not not_4 (not_4_out, register_1_q);
  // Digital_Oscilloscope digital_oscilloscope_1: pin names not known; wires that end beside it: clk_2x, register_1_q, digital_oscilloscope_1_p3, digital_oscilloscope_1_p4, digital_oscilloscope_1_p5, digital_oscilloscope_1_p6, enable, digital_oscilloscope_1_p8
  not not_5 (digital_oscilloscope_1_p8, rst_n);
  // Probe on rvr32_mc_1_mem_wdata
  rvr32_mc rvr32_mc_1 (
    .wdata(in_3), .wstrb(rvr32_lsu_1_mem_wstrb), .mem_rdata(rdata), .clk(not_4_out),
    .valid(digital_oscilloscope_1_p4), .clk_mem(not_1_out), .mem_wdata(rvr32_mc_1_mem_wdata),
    .rdata(rvr32_mc_1_rdata), .ready(digital_oscilloscope_1_p3), .mem_we(digital_oscilloscope_1_p6));  // open: addr, mem_addr, mem_ce
  rvr32_lsu rvr32_lsu_1 (
    .req(req), .clk(not_4_out), .rst_n(rst_n), .mem_ready(digital_oscilloscope_1_p3),
    .mem_rdata(rvr32_mc_1_rdata), .lsuop(in_4), .wdata(in_3), .mem_wstrb(rvr32_lsu_1_mem_wstrb),
    .ready(digital_oscilloscope_1_p5), .mem_valid(digital_oscilloscope_1_p4), .rdata(rvr32_lsu_1_rdata));  // open: addr, mem_addr, mem_wdata
  // Probe on rvr32_lsu_1_rdata
endmodule
